// Logisim project SCEVİK_SAYMİS_pro2.circ as structural Verilog: 23 circuits, main circuit main
module main (
  input  ready,
  input  [15:0] in_2,
  input  [15:0] in_3,
  input  ready_2,
  input  [15:0] in_5,
  input  [11:0] in_6
);

  wire _900_1_out, and_1_out, and_2_out, and_3_out, and_4_out, and_5_out, clock_1_int, clock_2_out,
       cpu2_1_intack, cpu2_1_memload, interruptinput_1_int, pic_1_active;
  wire [2:0] priority_encoder_1_out;
  wire [3:0] n16bi_treg_1_output_2, n16bi_treg_1_output_3, n16bi_treg_2_output_2;
  wire [7:0] n16bi_treg_1_output;
  wire [11:0] cpu2_1_addr, n16bi_treg_2_output;
  wire [15:0] clock_1_output, cpu2_1_dout, interruptinput_1_dout, multiplexer_1_out, multiplexer_2_out,
       pic_1_picout, polling_1_dout, ram_1_data;

  clock clock_1 (.clk(clock_2_out), .\int (clock_1_int), .\output (clock_1_output));
  Clock clock_2 (.out(clock_2_out));
  interruptinput interruptinput_1 (
    .Din(in_2), .ready(ready), .Dout(interruptinput_1_dout), .\int (interruptinput_1_int), .Addr(cpu2_1_addr));
  PIC pic_1 (.input1(interruptinput_1_int), .input2(clock_1_int), .active(pic_1_active), .PicOut(pic_1_picout));
  polling polling_1 (.Din(in_3), .ready(ready_2), .Dout(polling_1_dout), .Addr(cpu2_1_addr));
  Multiplexer #(.select(3), .width(16), .enable("false")) multiplexer_1 (
    .in0(in_5), .in1(polling_1_dout), .in2(interruptinput_1_dout), .in3(clock_1_output), .in4(ram_1_data),
    .out(multiplexer_1_out), .sel(priority_encoder_1_out));  // open: in5, in6, in7
  Multiplexer #(.width(16), .enable("false")) multiplexer_2 (
    .in0(multiplexer_1_out), .in1(pic_1_picout), .out(multiplexer_2_out), .sel(cpu2_1_intack));
  CPU2 cpu2_1 (
    .Din(multiplexer_2_out), .Dout(cpu2_1_dout), .\int (pic_1_active), .clk(clock_2_out), .Addr(cpu2_1_addr),
    .memload(cpu2_1_memload), .intack(cpu2_1_intack));
  and _900_1 (_900_1_out, cpu2_1_addr[11], ~cpu2_1_addr[10], ~cpu2_1_addr[9], cpu2_1_addr[8], ~cpu2_1_addr[7], ~cpu2_1_addr[6], ~cpu2_1_addr[5], ~cpu2_1_addr[4], ~cpu2_1_addr[3], ~cpu2_1_addr[2], ~cpu2_1_addr[1]);  // AND_Gate
  Priority_Encoder priority_encoder_1 (
    .in0(1'b1), .in1(_900_1_out), .in2(and_1_out), .in3(and_2_out), .in4(and_3_out),
    .out(priority_encoder_1_out), .en_in(1'b1));  // open: in5, in6, in7
  RAM #(.addrWidth(12), .dataWidth(16), .bus("separate")) ram_1 (
    .addr(cpu2_1_addr), .din(cpu2_1_dout), .data(ram_1_data), .str(cpu2_1_memload), .sel(1'b1), .ld(1'b1),
    .clr(1'b0));  // open: clk
  and and_1 (and_1_out, cpu2_1_addr[11], ~cpu2_1_addr[10], cpu2_1_addr[9], ~cpu2_1_addr[8], ~cpu2_1_addr[7], ~cpu2_1_addr[6], ~cpu2_1_addr[5], ~cpu2_1_addr[4], ~cpu2_1_addr[3], ~cpu2_1_addr[2], ~cpu2_1_addr[1], ~cpu2_1_addr[0]);  // AND_Gate
  and and_2 (and_2_out, cpu2_1_addr[11], ~cpu2_1_addr[10], cpu2_1_addr[9], cpu2_1_addr[8], ~cpu2_1_addr[7], ~cpu2_1_addr[6], cpu2_1_addr[5], ~cpu2_1_addr[4], ~cpu2_1_addr[3], ~cpu2_1_addr[2], cpu2_1_addr[1], cpu2_1_addr[0]);  // AND_Gate
  LED led_1 (.in(and_1_out));
  Hex_Digit_Display hex_digit_display_1 (.value(n16bi_treg_1_output_3));  // open: dp
  and and_3 (and_3_out, ~cpu2_1_addr[11], ~cpu2_1_addr[10]);  // AND_Gate
  Hex_Digit_Display hex_digit_display_2 (.value(n16bi_treg_1_output_2));  // open: dp
  Hex_Digit_Display hex_digit_display_3 (.value(n16bi_treg_1_output[7:4]));  // open: dp
  \_16BİTREG  \u_16bi̇treg_1  (
    .INPUT(cpu2_1_dout), .CLK(clock_2_out), .LOAD(and_4_out),
    .OUTPUT({n16bi_treg_1_output_3, n16bi_treg_1_output_2, n16bi_treg_1_output}));
  Hex_Digit_Display hex_digit_display_4 (.value(n16bi_treg_1_output[3:0]));  // open: dp
  and and_4 (and_4_out, cpu2_1_addr[11], ~cpu2_1_addr[10], cpu2_1_addr[9], cpu2_1_addr[8], ~cpu2_1_addr[7], ~cpu2_1_addr[6], ~cpu2_1_addr[5], ~cpu2_1_addr[4], ~cpu2_1_addr[3], ~cpu2_1_addr[2], ~cpu2_1_addr[1], ~cpu2_1_addr[0]);  // AND_Gate
  Hex_Digit_Display hex_digit_display_5 (.value(n16bi_treg_2_output_2));  // open: dp
  \_16BİTREG  \u_16bi̇treg_2  (
    .INPUT(cpu2_1_dout), .CLK(clock_2_out), .LOAD(and_5_out),
    .OUTPUT({n16bi_treg_2_output_2, n16bi_treg_2_output}));
  Hex_Digit_Display hex_digit_display_6 (.value(n16bi_treg_2_output[7:4]));  // open: dp
  Hex_Digit_Display hex_digit_display_7 (.value(n16bi_treg_2_output[11:8]));  // open: dp
  and and_5 (and_5_out, cpu2_1_addr[11], ~cpu2_1_addr[10], cpu2_1_addr[9], cpu2_1_addr[8], ~cpu2_1_addr[7], ~cpu2_1_addr[6], ~cpu2_1_addr[5], ~cpu2_1_addr[4], ~cpu2_1_addr[3], ~cpu2_1_addr[2], ~cpu2_1_addr[1], cpu2_1_addr[0]);  // AND_Gate
  Hex_Digit_Display hex_digit_display_8 (.value(n16bi_treg_2_output[3:0]));  // open: dp
endmodule

module ALU (
  input  [15:0] INPUT1,
  input  [15:0] INPUT2,
  input  [5:0] ALUOP,
  output ZF,
  output [15:0] OUTPUT
);

  wire and_2_out;
  wire [15:0] adder_1_out, adder_2_out, and_1_out, multiplexer_1_out, multiplexer_2_out, not_1_out, or_1_out,
       subtractor_1_out, subtractor_2_out, xor_1_out;

  Adder #(.width(16)) adder_1 (.a(INPUT1), .b(INPUT2), .out(adder_1_out));  // open: cin, cout
  Subtractor #(.width(16)) subtractor_1 (.a(INPUT1), .b(INPUT2), .out(subtractor_1_out));  // open: bin, bout
  assign and_1_out = INPUT1 & INPUT2;  // AND_Gate and_1, 16 bits wide
  assign or_1_out = INPUT1 | INPUT2;  // OR_Gate or_1, 16 bits wide
  assign not_1_out = ~INPUT2;  // NOT_Gate not_1, 16 bits wide
  Adder #(.width(16)) adder_2 (.a(INPUT2), .b(16'h1), .out(adder_2_out));  // open: cin, cout
  Subtractor #(.width(16)) subtractor_2 (.a(INPUT2), .b(16'h1), .out(subtractor_2_out));  // open: bin, bout
  assign xor_1_out = INPUT1 ^ INPUT2;  // XOR_Gate xor_1, 16 bits wide
  Multiplexer #(.select(3), .width(16), .enable("false")) multiplexer_1 (
    .in0(adder_1_out), .in1(subtractor_1_out), .in2(and_1_out), .in3(or_1_out), .in4(xor_1_out),
    .out(multiplexer_1_out), .sel(ALUOP[5:3]));  // open: in5, in6, in7
  Multiplexer #(.select(3), .width(16), .enable("false")) multiplexer_2 (
    .in0(not_1_out), .in1(INPUT2), .in2(adder_2_out), .in3(subtractor_2_out), .out(multiplexer_2_out),
    .sel(ALUOP[2:0]));  // open: in4, in5, in6, in7
  and and_2 (and_2_out, ALUOP[3], ALUOP[4], ALUOP[5]);
  Multiplexer #(.width(16), .enable("false")) multiplexer_3 (
    .in0(multiplexer_1_out), .in1(multiplexer_2_out), .out(OUTPUT), .sel(and_2_out));
  nor nor_1 (ZF, OUTPUT[0], OUTPUT[1], OUTPUT[2], OUTPUT[3], OUTPUT[4], OUTPUT[5], OUTPUT[6], OUTPUT[7], OUTPUT[8], OUTPUT[9], OUTPUT[10], OUTPUT[11], OUTPUT[12], OUTPUT[13], OUTPUT[14], OUTPUT[15]);
endmodule

module \_16BİTREG  (
  input  [15:0] INPUT,
  input  CLK,
  input  LOAD,
  output [15:0] OUTPUT
);

  wire not_1_out, not_2_out, not_3_out, not_4_out, not_5_out, not_6_out, not_7_out, not_8_out, not_9_out,
       not_10_out, not_11_out, not_12_out, not_13_out, not_14_out, not_15_out, not_16_out;

  S_R_Flip_Flop s_r_ff_1 (.S(INPUT[0]), .clk(CLK), .R(not_1_out), .Q(OUTPUT[0]), .en(LOAD));  // open: Qn, preset, reset
  not not_1 (not_1_out, INPUT[0]);
  S_R_Flip_Flop s_r_ff_2 (.S(INPUT[1]), .clk(CLK), .R(not_2_out), .Q(OUTPUT[1]), .en(LOAD));  // open: Qn, preset, reset
  not not_2 (not_2_out, INPUT[1]);
  S_R_Flip_Flop s_r_ff_3 (.S(INPUT[2]), .clk(CLK), .R(not_3_out), .Q(OUTPUT[2]), .en(LOAD));  // open: Qn, preset, reset
  not not_3 (not_3_out, INPUT[2]);
  S_R_Flip_Flop s_r_ff_4 (.S(INPUT[3]), .clk(CLK), .R(not_4_out), .Q(OUTPUT[3]), .en(LOAD));  // open: Qn, preset, reset
  not not_4 (not_4_out, INPUT[3]);
  S_R_Flip_Flop s_r_ff_5 (.S(INPUT[4]), .clk(CLK), .R(not_5_out), .Q(OUTPUT[4]), .en(LOAD));  // open: Qn, preset, reset
  not not_5 (not_5_out, INPUT[4]);
  S_R_Flip_Flop s_r_ff_6 (.S(INPUT[5]), .clk(CLK), .R(not_6_out), .Q(OUTPUT[5]), .en(LOAD));  // open: Qn, preset, reset
  not not_6 (not_6_out, INPUT[5]);
  S_R_Flip_Flop s_r_ff_7 (.S(INPUT[6]), .clk(CLK), .R(not_7_out), .Q(OUTPUT[6]), .en(LOAD));  // open: Qn, preset, reset
  not not_7 (not_7_out, INPUT[6]);
  S_R_Flip_Flop s_r_ff_8 (.S(INPUT[7]), .clk(CLK), .R(not_8_out), .Q(OUTPUT[7]), .en(LOAD));  // open: Qn, preset, reset
  not not_8 (not_8_out, INPUT[7]);
  S_R_Flip_Flop s_r_ff_9 (.S(INPUT[8]), .clk(CLK), .R(not_9_out), .Q(OUTPUT[8]), .en(LOAD));  // open: Qn, preset, reset
  not not_9 (not_9_out, INPUT[8]);
  S_R_Flip_Flop s_r_ff_10 (
    .S(INPUT[9]), .clk(CLK), .R(not_10_out), .Q(OUTPUT[9]), .en(LOAD));  // open: Qn, preset, reset
  not not_10 (not_10_out, INPUT[9]);
  S_R_Flip_Flop s_r_ff_11 (
    .S(INPUT[10]), .clk(CLK), .R(not_11_out), .Q(OUTPUT[10]), .en(LOAD));  // open: Qn, preset, reset
  not not_11 (not_11_out, INPUT[10]);
  S_R_Flip_Flop s_r_ff_12 (
    .S(INPUT[11]), .clk(CLK), .R(not_12_out), .Q(OUTPUT[11]), .en(LOAD));  // open: Qn, preset, reset
  not not_12 (not_12_out, INPUT[11]);
  S_R_Flip_Flop s_r_ff_13 (
    .S(INPUT[12]), .clk(CLK), .R(not_13_out), .Q(OUTPUT[12]), .en(LOAD));  // open: Qn, preset, reset
  not not_13 (not_13_out, INPUT[12]);
  S_R_Flip_Flop s_r_ff_14 (
    .S(INPUT[13]), .clk(CLK), .R(not_14_out), .Q(OUTPUT[13]), .en(LOAD));  // open: Qn, preset, reset
  not not_14 (not_14_out, INPUT[13]);
  S_R_Flip_Flop s_r_ff_15 (
    .S(INPUT[14]), .clk(CLK), .R(not_15_out), .Q(OUTPUT[14]), .en(LOAD));  // open: Qn, preset, reset
  not not_15 (not_15_out, INPUT[14]);
  S_R_Flip_Flop s_r_ff_16 (
    .S(INPUT[15]), .clk(CLK), .R(not_16_out), .Q(OUTPUT[15]), .en(LOAD));  // open: Qn, preset, reset
  not not_16 (not_16_out, INPUT[15]);
endmodule

module REGBANK (
  input  LOAD,
  input  [15:0] DataIn,
  input  [2:0] regSelect,
  input  sti,
  input  cli,
  input  flagload,
  input  zf,
  input  zfload,
  input  CLK,
  input  SP_plus_plus,
  input  SP_minus_minus,
  output [15:0] Reg0,
  output [15:0] Reg1,
  output [15:0] Reg2,
  output [15:0] Reg3,
  output [15:0] Reg4,
  output [15:0] Reg5,
  output [15:0] Reg6,
  output [15:0] Reg7,
  output zfout,
  output IF
);

  wire and_1_out, and_2_out, and_3_out, and_4_out, and_5_out, and_6_out, and_7_out, and_8_out,
       decoder_1_out0, decoder_1_out1, decoder_1_out2, decoder_1_out3, decoder_1_out4, decoder_1_out5,
       decoder_1_out6, decoder_1_out7, or_1_out, or_2_out, or_3_out;

  Decoder #(.select(3), .enable("false")) decoder_1 (
    .out0(decoder_1_out0), .out1(decoder_1_out1), .out2(decoder_1_out2), .out3(decoder_1_out3),
    .out4(decoder_1_out4), .out5(decoder_1_out5), .out6(decoder_1_out6), .out7(decoder_1_out7),
    .sel(regSelect));
  and and_1 (and_1_out, decoder_1_out7, LOAD);
  or or_1 (or_1_out, SP_minus_minus, SP_plus_plus);
  and and_2 (and_2_out, decoder_1_out0, LOAD);
  and and_3 (and_3_out, decoder_1_out1, LOAD);
  and and_4 (and_4_out, decoder_1_out2, LOAD);
  and and_5 (and_5_out, decoder_1_out3, LOAD);
  and and_6 (and_6_out, decoder_1_out4, LOAD);
  and and_7 (and_7_out, decoder_1_out5, LOAD);
  and and_8 (and_8_out, decoder_1_out6, LOAD);
  or or_2 (or_2_out, and_1_out, or_1_out);
  or or_3 (or_3_out, and_8_out, flagload);
  \_16BİTREG  \u_16bi̇treg_1  (.INPUT(DataIn), .CLK(CLK), .LOAD(and_2_out), .OUTPUT(Reg0));
  \_16BİTREG  \u_16bi̇treg_2  (.INPUT(DataIn), .CLK(CLK), .LOAD(and_3_out), .OUTPUT(Reg1));
  \_16BİTREG  \u_16bi̇treg_3  (.INPUT(DataIn), .CLK(CLK), .LOAD(and_4_out), .OUTPUT(Reg2));
  \_16BİTREG  \u_16bi̇treg_4  (.INPUT(DataIn), .CLK(CLK), .LOAD(and_5_out), .OUTPUT(Reg3));
  \_16BİTREG  \u_16bi̇treg_5  (.INPUT(DataIn), .CLK(CLK), .LOAD(and_6_out), .OUTPUT(Reg4));
  \_16BİTREG  \u_16bi̇treg_6  (.INPUT(DataIn), .CLK(CLK), .LOAD(and_7_out), .OUTPUT(Reg5));
  _6_reg u_6_reg_1 (
    .ZF(zf), .zfload(zfload), .flagload(or_3_out), .clk(CLK), .Din(DataIn), .CLI(cli), .STI(sti),
    .ZFout(zfout), .Dout(Reg6), .IF(IF));
  SPREG spreg_1 (
    .INPUT(DataIn), .CLK(CLK), .LOAD(or_2_out), .SP_plus_plus(SP_plus_plus), .SP_minus_minus(SP_minus_minus),
    .OUTPUT(Reg7));
endmodule

module SPREG (
  input  [15:0] INPUT,
  input  CLK,
  input  LOAD,
  input  SP_plus_plus,
  input  SP_minus_minus,
  output [15:0] OUTPUT
);

  wire or_1_out;
  wire [15:0] adder_1_out, multiplexer_1_out, subtractor_1_out;

  Multiplexer #(.select(2), .width(16), .enable("false")) multiplexer_1 (
    .in0(INPUT), .in1(adder_1_out), .in2(subtractor_1_out), .out(multiplexer_1_out),
    .sel({SP_minus_minus, SP_plus_plus}));  // open: in3
  or or_1 (or_1_out, SP_plus_plus, SP_minus_minus, LOAD);
  \_16BİTREG  \u_16bi̇treg_1  (.INPUT(multiplexer_1_out), .CLK(CLK), .LOAD(or_1_out), .OUTPUT(OUTPUT));
  Subtractor #(.width(16)) subtractor_1 (.a(OUTPUT), .b(16'h1), .out(subtractor_1_out));  // open: bin, bout
  Adder #(.width(16)) adder_1 (.a(OUTPUT), .b(16'h1), .out(adder_1_out));  // open: cin, cout
endmodule

module _12BITREG (
  input  [11:0] INPUT,
  input  CLK,
  input  LOAD,
  output [11:0] OUTPUT
);

  wire not_1_out, not_2_out, not_3_out, not_4_out, not_5_out, not_6_out, not_7_out, not_8_out, not_9_out,
       not_10_out, not_11_out, not_12_out;

  S_R_Flip_Flop s_r_ff_1 (.S(INPUT[0]), .clk(CLK), .R(not_1_out), .Q(OUTPUT[0]), .en(LOAD));  // open: Qn, preset, reset
  not not_1 (not_1_out, INPUT[0]);
  S_R_Flip_Flop s_r_ff_2 (.S(INPUT[1]), .clk(CLK), .R(not_2_out), .Q(OUTPUT[1]), .en(LOAD));  // open: Qn, preset, reset
  not not_2 (not_2_out, INPUT[1]);
  S_R_Flip_Flop s_r_ff_3 (.S(INPUT[2]), .clk(CLK), .R(not_3_out), .Q(OUTPUT[2]), .en(LOAD));  // open: Qn, preset, reset
  not not_3 (not_3_out, INPUT[2]);
  S_R_Flip_Flop s_r_ff_4 (.S(INPUT[3]), .clk(CLK), .R(not_4_out), .Q(OUTPUT[3]), .en(LOAD));  // open: Qn, preset, reset
  not not_4 (not_4_out, INPUT[3]);
  S_R_Flip_Flop s_r_ff_5 (.S(INPUT[4]), .clk(CLK), .R(not_5_out), .Q(OUTPUT[4]), .en(LOAD));  // open: Qn, preset, reset
  not not_5 (not_5_out, INPUT[4]);
  S_R_Flip_Flop s_r_ff_6 (.S(INPUT[5]), .clk(CLK), .R(not_6_out), .Q(OUTPUT[5]), .en(LOAD));  // open: Qn, preset, reset
  not not_6 (not_6_out, INPUT[5]);
  S_R_Flip_Flop s_r_ff_7 (.S(INPUT[6]), .clk(CLK), .R(not_7_out), .Q(OUTPUT[6]), .en(LOAD));  // open: Qn, preset, reset
  not not_7 (not_7_out, INPUT[6]);
  S_R_Flip_Flop s_r_ff_8 (.S(INPUT[7]), .clk(CLK), .R(not_8_out), .Q(OUTPUT[7]), .en(LOAD));  // open: Qn, preset, reset
  not not_8 (not_8_out, INPUT[7]);
  S_R_Flip_Flop s_r_ff_9 (.S(INPUT[8]), .clk(CLK), .R(not_9_out), .Q(OUTPUT[8]), .en(LOAD));  // open: Qn, preset, reset
  not not_9 (not_9_out, INPUT[8]);
  S_R_Flip_Flop s_r_ff_10 (
    .S(INPUT[9]), .clk(CLK), .R(not_10_out), .Q(OUTPUT[9]), .en(LOAD));  // open: Qn, preset, reset
  not not_10 (not_10_out, INPUT[9]);
  S_R_Flip_Flop s_r_ff_11 (
    .S(INPUT[10]), .clk(CLK), .R(not_11_out), .Q(OUTPUT[10]), .en(LOAD));  // open: Qn, preset, reset
  not not_11 (not_11_out, INPUT[10]);
  S_R_Flip_Flop s_r_ff_12 (
    .S(INPUT[11]), .clk(CLK), .R(not_12_out), .Q(OUTPUT[11]), .en(LOAD));  // open: Qn, preset, reset
  not not_12 (not_12_out, INPUT[11]);
endmodule

module PC (
  input  [11:0] INPUT,
  input  CLK,
  input  LOAD,
  input  INC,
  output [11:0] OUTPUT
);

  wire or_1_out;
  wire [11:0] adder_1_out, multiplexer_1_out;

  Multiplexer #(.width(12), .enable("false")) multiplexer_1 (
    .in0(INPUT), .in1(adder_1_out), .out(multiplexer_1_out), .sel(INC));
  or or_1 (or_1_out, INC, LOAD);
  _12BITREG u_12bitreg_1 (.INPUT(multiplexer_1_out), .CLK(CLK), .LOAD(or_1_out), .OUTPUT(OUTPUT));
  Adder #(.width(12)) adder_1 (.a(OUTPUT), .b(12'h1), .out(adder_1_out));  // open: cin, cout
endmodule

module _1BITREG (
  input  CLK,
  input  INPUT,
  input  LOAD,
  output OUTPUT
);

  wire not_1_out;

  S_R_Flip_Flop s_r_ff_1 (.S(INPUT), .clk(CLK), .R(not_1_out), .Q(OUTPUT), .en(LOAD));  // open: Qn, preset, reset
  not not_1 (not_1_out, INPUT);
endmodule

module _4BITREG (
  input  [3:0] INPUT,
  input  CLK,
  input  LOAD,
  output [3:0] OUTPUT
);

  wire not_1_out, not_2_out, not_3_out, not_4_out;

  S_R_Flip_Flop s_r_ff_1 (.S(INPUT[0]), .clk(CLK), .R(not_1_out), .Q(OUTPUT[0]), .en(LOAD));  // open: Qn, preset, reset
  not not_1 (not_1_out, INPUT[0]);
  S_R_Flip_Flop s_r_ff_2 (.S(INPUT[1]), .clk(CLK), .R(not_2_out), .Q(OUTPUT[1]), .en(LOAD));  // open: Qn, preset, reset
  not not_2 (not_2_out, INPUT[1]);
  S_R_Flip_Flop s_r_ff_3 (.S(INPUT[2]), .clk(CLK), .R(not_3_out), .Q(OUTPUT[2]), .en(LOAD));  // open: Qn, preset, reset
  not not_3 (not_3_out, INPUT[2]);
  S_R_Flip_Flop s_r_ff_4 (.S(INPUT[3]), .clk(CLK), .R(not_4_out), .Q(OUTPUT[3]), .en(LOAD));  // open: Qn, preset, reset
  not not_4 (not_4_out, INPUT[3]);
endmodule

module _5BITREG (
  input  [4:0] INPUT,
  input  CLK,
  input  LOAD,
  output [4:0] OUTPUT
);

  wire not_1_out, not_2_out, not_3_out, not_4_out, not_5_out;

  S_R_Flip_Flop s_r_ff_1 (.S(INPUT[0]), .clk(CLK), .R(not_1_out), .Q(OUTPUT[0]), .en(LOAD));  // open: Qn, preset, reset
  not not_1 (not_1_out, INPUT[0]);
  S_R_Flip_Flop s_r_ff_2 (.S(INPUT[1]), .clk(CLK), .R(not_2_out), .Q(OUTPUT[1]), .en(LOAD));  // open: Qn, preset, reset
  not not_2 (not_2_out, INPUT[1]);
  S_R_Flip_Flop s_r_ff_3 (.S(INPUT[2]), .clk(CLK), .R(not_3_out), .Q(OUTPUT[2]), .en(LOAD));  // open: Qn, preset, reset
  not not_3 (not_3_out, INPUT[2]);
  S_R_Flip_Flop s_r_ff_4 (.S(INPUT[3]), .clk(CLK), .R(not_4_out), .Q(OUTPUT[3]), .en(LOAD));  // open: Qn, preset, reset
  not not_4 (not_4_out, INPUT[3]);
  S_R_Flip_Flop s_r_ff_5 (.S(INPUT[4]), .clk(CLK), .R(not_5_out), .Q(OUTPUT[4]), .en(LOAD));  // open: Qn, preset, reset
  not not_5 (not_5_out, INPUT[4]);
endmodule

module CPU (
);

  wire alu_1_zf, clock_1_out;
  wire [1:0] n1bitreg_1_output;
  wire [4:0] multiplexer_6_out, multiplexer_7_out, n5bitreg_1_output, rom_1_data_2;
  wire [11:0] adder_1_out, multiplexer_1_out, multiplexer_2_out, multiplexer_5_out, pc_1_output,
       regbank_1_p3, regbank_1_p13;
  wire [15:0] alu_1_output, multiplexer_3_out, ram_1_data, regbank_1_p2, regbank_1_p6, regbank_1_p7,
       regbank_1_p8, regbank_1_p9, regbank_1_p10, regbank_1_p11, regbank_1_p12;
  wire [15:12] multiplexer_5_out_2, regbank_1_p13_2;
  wire [19:5] rom_1_data;

  Multiplexer #(.width(12), .enable("false")) multiplexer_1 (
    .in0(adder_1_out), .in1(ram_1_data[11:0]), .out(multiplexer_1_out), .sel(rom_1_data[19]));
  Clock clock_1 (.out(clock_1_out));
  PC pc_1 (
    .INPUT(multiplexer_1_out), .CLK(clock_1_out), .LOAD(rom_1_data[16]), .INC(rom_1_data[15]),
    .OUTPUT(pc_1_output));
  Adder #(.width(12)) adder_1 (.a(pc_1_output), .b(regbank_1_p3), .out(adder_1_out));  // open: cin, cout
  Multiplexer #(.select(2), .width(12), .enable("false")) multiplexer_2 (
    .in0(pc_1_output), .in1(multiplexer_5_out), .in2(regbank_1_p13), .out(multiplexer_2_out),
    .sel(rom_1_data[12:11]));  // open: in3
  RAM #(.addrWidth(12), .dataWidth(16), .bus("separate")) ram_1 (
    .addr(multiplexer_2_out), .din(regbank_1_p2), .data(ram_1_data), .str(rom_1_data[8]), .sel(1'b1),
    .clk(clock_1_out), .ld(1'b1), .clr(1'b0));
  // REGBANK regbank_1: pin names not known; wires that end beside it: rom_1_data[5], regbank_1_p2, regbank_1_p3[2:0], clock_1_out, rom_1_data[6], regbank_1_p6, regbank_1_p7, regbank_1_p8, regbank_1_p9, regbank_1_p10, regbank_1_p11, regbank_1_p12, {regbank_1_p13_2, regbank_1_p13}, rom_1_data[7], rom_1_data[7], rom_1_data[7]
  isJZ isjz_1 (.in_1(ram_1_data[15:12]), .jz(n1bitreg_1_output[1]));
  Multiplexer #(.select(3), .width(16), .enable("false")) multiplexer_3 (
    .in0(regbank_1_p6), .in1(regbank_1_p7), .in2(regbank_1_p8), .in3(regbank_1_p9), .in4(regbank_1_p10),
    .in5(regbank_1_p11), .in6(regbank_1_p12), .in7({regbank_1_p13_2, regbank_1_p13}),
    .out(multiplexer_3_out), .sel(regbank_1_p3[8:6]));
  Multiplexer #(.select(3), .width(16), .enable("false")) multiplexer_4 (
    .in0(ram_1_data), .in1(multiplexer_3_out), .in2({multiplexer_5_out_2, multiplexer_5_out}),
    .in3(alu_1_output), .in4({4'b0000, pc_1_output}), .out(regbank_1_p2),
    .sel({rom_1_data[18], rom_1_data[10:9]}));  // open: in5, in6, in7
  ALU alu_1 (
    .INPUT1(multiplexer_3_out), .INPUT2({multiplexer_5_out_2, multiplexer_5_out}),
    .ALUOP(regbank_1_p3[11:6]), .ZF(alu_1_zf), .OUTPUT(alu_1_output));
  Multiplexer #(.select(3), .width(16), .enable("false")) multiplexer_5 (
    .in0(regbank_1_p6), .in1(regbank_1_p7), .in2(regbank_1_p8), .in3(regbank_1_p9), .in4(regbank_1_p10),
    .in5(regbank_1_p11), .in6(regbank_1_p12), .in7({regbank_1_p13_2, regbank_1_p13}),
    .out({multiplexer_5_out_2, multiplexer_5_out}), .sel(regbank_1_p3[5:3]));
  _12BITREG u_12bitreg_1 (.INPUT(ram_1_data[11:0]), .CLK(clock_1_out), .LOAD(rom_1_data[13]), .OUTPUT(regbank_1_p3));
  _1BITREG u_1bitreg_1 (.CLK(clock_1_out), .INPUT(alu_1_zf), .LOAD(rom_1_data[14]), .OUTPUT(n1bitreg_1_output[0]));
  Multiplexer #(.width(5), .enable("false")) multiplexer_6 (
    .in0(rom_1_data_2), .in1(multiplexer_7_out), .out(multiplexer_6_out), .sel(rom_1_data[17]));
  Multiplexer #(.select(2), .width(5), .enable("false")) multiplexer_7 (
    .in0({ram_1_data[15:12], 1'b0}), .in1({ram_1_data[15:12], 1'b0}), .in2({5{1'b0}}), .in3(5'b01010),
    .out(multiplexer_7_out), .sel(n1bitreg_1_output));
  _5BITREG u_5bitreg_1 (.INPUT(multiplexer_6_out), .CLK(clock_1_out), .LOAD(1'b1), .OUTPUT(n5bitreg_1_output));
  ROM #(.addrWidth(5), .dataWidth(20)) rom_1 (
    .addr(n5bitreg_1_output), .data({rom_1_data, rom_1_data_2}));  // open: sel

  // Notes on the sheet:
  //   contents of rom_1 (hex, n*v repeats v):
  //   2a000 0 8020 0 820 0 b00 0 0 0 10000 0 0 0 4620 0 1380 0 53 1020 51180 0 57 91000
  //   Next Address
endmodule

module isJZ (
  input  [3:0] in_1,
  output jz
);

  wire not_1_out, not_2_out, not_3_out;

  not not_1 (not_1_out, in_1[0]);
  not not_2 (not_2_out, in_1[1]);
  not not_3 (not_3_out, in_1[3]);
  and and_1 (jz, not_1_out, not_2_out, in_1[2], not_3_out);
endmodule

module _6_reg (
  input  ZF,
  input  zfload,
  input  [15:0] Din,
  input  CLI,
  input  STI,
  input  flagload,
  input  clk,
  output ZFout,
  output [15:0] Dout,
  output IF
);

  wire and_1_out, and_2_out, and_3_out, and_5_out, and_6_out, and_7_out, and_8_out, and_9_out, or_1_out,
       or_2_out, or_3_out, or_4_out;

  and and_1 (and_1_out, zfload, ~ZF);  // AND_Gate
  and and_2 (and_2_out, Din[0], flagload);
  and and_3 (and_3_out, ~Din[0], flagload);  // AND_Gate
  // AND_Gate and_4 has open pins: in0=1'b0, in1=CLI, out=open
  and and_5 (and_5_out, CLI, 1'b1);
  and and_6 (and_6_out, Din[1], flagload);
  and and_7 (and_7_out, ~Din[1], flagload);  // AND_Gate
  and and_8 (and_8_out, zfload, ZF);
  and and_9 (and_9_out, 1'b1, STI);
  or or_1 (or_1_out, and_8_out, and_2_out);
  or or_2 (or_2_out, and_1_out, and_3_out);
  // AND_Gate and_10 has open pins: in0=STI, in1=1'b0, out=open
  or or_3 (or_3_out, and_9_out, and_6_out);
  or or_4 (or_4_out, and_5_out, and_7_out);
  _1BITREG u_1bitreg_1 (.CLK(clk), .INPUT(Din[2]), .LOAD(flagload), .OUTPUT(Dout[2]));
  _4BITREG u_4bitreg_1 (.INPUT(Din[7:4]), .CLK(clk), .LOAD(flagload), .OUTPUT(Dout[7:4]));
  _4BITREG u_4bitreg_2 (.INPUT(Din[11:8]), .CLK(clk), .LOAD(flagload), .OUTPUT(Dout[11:8]));
  _4BITREG u_4bitreg_3 (.INPUT(Din[15:12]), .CLK(clk), .LOAD(flagload), .OUTPUT(Dout[15:12]));
  _1BITREG u_1bitreg_2 (.CLK(clk), .INPUT(Din[3]), .LOAD(flagload), .OUTPUT(Dout[3]));
  S_R_Flip_Flop u_Zf (.S(or_1_out), .clk(clk), .R(or_2_out), .Q(Dout[0]));  // open: Qn, preset, reset, en
  S_R_Flip_Flop u_IF (.S(or_3_out), .clk(clk), .R(or_4_out), .Q(Dout[1]));  // open: Qn, preset, reset, en

  assign IF = Dout[1];
  assign ZFout = Dout[0];
endmodule

module encoder (
  input  _0,
  input  _1,
  input  _2,
  input  _3,
  output [1:0] out_5
);

  wire priority_encoder_1_gs;
  wire [1:0] priority_encoder_1_out;

  Priority_Encoder #(.select(2)) priority_encoder_1 (
    .in0(_0), .in1(_1), .in2(_2), .in3(_3), .out(priority_encoder_1_out), .gs(priority_encoder_1_gs));  // open: en_out, en_in
  Multiplexer #(.width(2), .enable("false")) multiplexer_1 (
    .in0(2'b00), .in1(priority_encoder_1_out), .out(out_5), .sel(priority_encoder_1_gs));
endmodule

module cu (
  input  [15:0] Din,
  input  ZF,
  input  IF,
  input  INT,
  input  clk,
  output FETCH,
  output ARMUX0,
  output ARMUX1,
  output PcLD,
  output PC_plus_plus,
  output MEMLD,
  output REGLD,
  output zfload,
  output MUX0,
  output MUX1,
  output MUX2,
  output SP_minus_minus,
  output SP_plus_plus,
  output IRLD,
  output RETMUX,
  output intload,
  output flagload,
  output sti,
  output cli,
  output intack
);

  wire and_1_out, and_3_out;
  wire [0:0] and_2_out;
  wire [3:0] multiplexer_1_out;
  wire [4:0] multiplexer_2_out, multiplexer_3_out, n5bitreg_1_output, rom_1_data;

  and and_1 (and_1_out, ~rom_1_data[0], ~rom_1_data[1], ~rom_1_data[2], ~rom_1_data[3], ~rom_1_data[4]);  // AND_Gate
  and and_2 (and_2_out[0], ~Din[12], ~Din[13], Din[14], ~Din[15]);  // AND_Gate
  and and_3 (and_3_out, IF, INT, and_1_out);
  Multiplexer #(.select(2), .width(4), .enable("false")) multiplexer_1 (
    .in0(Din[15:12]), .in1(Din[15:12]), .in2(4'b0000), .in3(4'b0101), .out(multiplexer_1_out),
    .sel({ZF, and_2_out[0]}));
  Multiplexer #(.width(5), .enable("false")) multiplexer_2 (
    .in0({1'b0, multiplexer_1_out}), .in1(rom_1_data), .out(multiplexer_2_out), .sel(FETCH));
  Multiplexer #(.width(5), .enable("false")) multiplexer_3 (
    .in0(multiplexer_2_out), .in1(5'b10011), .out(multiplexer_3_out), .sel(and_3_out));
  _5BITREG u_5bitreg_1 (.INPUT(multiplexer_3_out), .CLK(clk), .LOAD(1'b1), .OUTPUT(n5bitreg_1_output));
  ROM #(.addrWidth(5), .dataWidth(25)) rom_1 (
    .addr(n5bitreg_1_output),
    .data({FETCH, ARMUX0, ARMUX1, PcLD, PC_plus_plus, MEMLD, REGLD, zfload, MUX0, MUX1, MUX2, SP_minus_minus, SP_plus_plus, IRLD, RETMUX, intload, flagload, sti, cli, intack, rom_1_data}));  // open: sel

  // Notes on the sheet:
  //   contents of rom_1 (hex, n*v repeats v):
  //   1100800 140000 840000 890000 0 200000 0 78000 492000 100f 686000 1010 80 40 1011 440000 600400
  //   601412 400100 496014 486235 e00440
endmodule

module newCPU (
);

  wire alu_1_zf, clock_1_out, cu_1_memld, cu_1_pc_plus_plus, cu_1_pcld, cu_1_regld, n1bitreg_1_output,
       undriven, undriven_3, undriven_4;
  wire [1:0] cu_1_armux0;
  wire [2:0] undriven_2;
  wire [11:0] adder_1_out, multiplexer_1_out, multiplexer_2_out, multiplexer_5_out, n12bitreg_1_output,
       pc_1_output, regbank_1_reg7;
  wire [15:0] alu_1_output, multiplexer_3_out, multiplexer_4_out, ram_1_data, regbank_1_reg0, regbank_1_reg1,
       regbank_1_reg2, regbank_1_reg3, regbank_1_reg4, regbank_1_reg5, regbank_1_reg6;
  wire [15:12] multiplexer_5_out_2, regbank_1_reg7_2;

  Multiplexer #(.width(12), .enable("false")) multiplexer_1 (
    .in0(adder_1_out), .in1(ram_1_data[11:0]), .out(multiplexer_1_out), .sel(undriven));
  Clock clock_1 (.out(clock_1_out));
  PC pc_1 (
    .INPUT(multiplexer_1_out), .CLK(clock_1_out), .LOAD(cu_1_pcld), .INC(cu_1_pc_plus_plus),
    .OUTPUT(pc_1_output));
  Adder #(.width(12)) adder_1 (.a(pc_1_output), .b(n12bitreg_1_output), .out(adder_1_out));  // open: cin, cout
  Multiplexer #(.select(2), .width(12), .enable("false")) multiplexer_2 (
    .in0(pc_1_output), .in1(multiplexer_5_out), .in2(regbank_1_reg7), .out(multiplexer_2_out),
    .sel(cu_1_armux0));  // open: in3
  RAM #(.addrWidth(12), .dataWidth(16), .bus("separate")) ram_1 (
    .addr(multiplexer_2_out), .din(multiplexer_4_out), .data(ram_1_data), .str(cu_1_memld), .sel(1'b1),
    .clk(clock_1_out), .ld(1'b1), .clr(1'b0));
  REGBANK regbank_1 (
    .LOAD(cu_1_regld), .DataIn(multiplexer_4_out), .regSelect(n12bitreg_1_output[2:0]), .CLK(clock_1_out),
    .Reg0(regbank_1_reg0), .Reg1(regbank_1_reg1), .Reg2(regbank_1_reg2), .Reg3(regbank_1_reg3),
    .Reg4(regbank_1_reg4), .Reg5(regbank_1_reg5), .Reg6(regbank_1_reg6),
    .Reg7({regbank_1_reg7_2, regbank_1_reg7}));  // open: sti, cli, flagload, SP_plus_plus, zf, zfload, zfout, IF, SP_minus_minus
  Multiplexer #(.select(3), .width(16), .enable("false")) multiplexer_3 (
    .in0(regbank_1_reg0), .in1(regbank_1_reg1), .in2(regbank_1_reg2), .in3(regbank_1_reg3),
    .in4(regbank_1_reg4), .in5(regbank_1_reg5), .in6(regbank_1_reg6),
    .in7({regbank_1_reg7_2, regbank_1_reg7}), .out(multiplexer_3_out), .sel(n12bitreg_1_output[8:6]));
  Multiplexer #(.select(3), .width(16), .enable("false")) multiplexer_4 (
    .in0(ram_1_data), .in1(multiplexer_3_out), .in2({multiplexer_5_out_2, multiplexer_5_out}),
    .in3(alu_1_output), .in4({4'b0000, pc_1_output}), .out(multiplexer_4_out), .sel(undriven_2));  // open: in5, in6, in7
  ALU alu_1 (
    .INPUT1(multiplexer_3_out), .INPUT2({multiplexer_5_out_2, multiplexer_5_out}),
    .ALUOP(n12bitreg_1_output[11:6]), .ZF(alu_1_zf), .OUTPUT(alu_1_output));
  Multiplexer #(.select(3), .width(16), .enable("false")) multiplexer_5 (
    .in0(regbank_1_reg0), .in1(regbank_1_reg1), .in2(regbank_1_reg2), .in3(regbank_1_reg3),
    .in4(regbank_1_reg4), .in5(regbank_1_reg5), .in6(regbank_1_reg6),
    .in7({regbank_1_reg7_2, regbank_1_reg7}), .out({multiplexer_5_out_2, multiplexer_5_out}),
    .sel(n12bitreg_1_output[5:3]));
  _12BITREG u_12bitreg_1 (.INPUT(ram_1_data[11:0]), .CLK(clock_1_out), .LOAD(undriven_3), .OUTPUT(n12bitreg_1_output));
  _1BITREG u_1bitreg_1 (.CLK(clock_1_out), .INPUT(alu_1_zf), .LOAD(undriven_4), .OUTPUT(n1bitreg_1_output));
  cu cu_1 (
    .Din(ram_1_data), .ARMUX0(cu_1_armux0[0]), .ARMUX1(cu_1_armux0[1]), .PcLD(cu_1_pcld),
    .PC_plus_plus(cu_1_pc_plus_plus), .MEMLD(cu_1_memld), .REGLD(cu_1_regld));  // open: ZF, IF, INT, clk, FETCH, zfload, MUX0, MUX1, MUX2, SP_minus_minus, SP_plus_plus, IRLD, RETMUX, intload, flagload, sti, cli, intack
endmodule

// CPU
module CPU2 (
  input  [15:0] Din,
  input  \int ,
  input  clk,
  output [11:0] Addr,
  output memload,
  output [15:0] Dout,
  output intack
);

  wire alu_1_zf, cu_1_cli, cu_1_flagload, cu_1_intload, cu_1_irld, cu_1_pc_plus_plus, cu_1_pcld, cu_1_regld,
       cu_1_retmux, cu_1_sp_minus_minus, cu_1_sp_plus_plus, cu_1_sti, cu_1_zfload, regbank_1_if,
       regbank_1_zfout;
  wire [1:0] cu_1_armux0;
  wire [2:0] cu_1_mux0;
  wire [11:0] adder_1_out, multiplexer_1_out, multiplexer_5_out, n12bitreg_1_output, n16bi_treg_1_output,
       pc_1_output, regbank_1_reg7;
  wire [15:0] adder_2_out, alu_1_output, multiplexer_4_out, regbank_1_reg0, regbank_1_reg1, regbank_1_reg2,
       regbank_1_reg3, regbank_1_reg4, regbank_1_reg5, regbank_1_reg6;
  wire [15:12] multiplexer_5_out_2, n16bi_treg_1_output_2, regbank_1_reg7_2;

  Multiplexer #(.width(12), .enable("false")) multiplexer_1 (
    .in0(adder_1_out), .in1(Din[11:0]), .out(multiplexer_1_out), .sel(cu_1_retmux));
  Adder #(.width(12)) adder_1 (.a(pc_1_output), .b(n12bitreg_1_output), .out(adder_1_out));  // open: cin, cout
  Multiplexer #(.select(2), .width(12), .enable("false")) multiplexer_2 (
    .in0(pc_1_output), .in1(multiplexer_5_out), .in2(regbank_1_reg7), .in3(n16bi_treg_1_output), .out(Addr),
    .sel(cu_1_armux0));
  PC pc_1 (.INPUT(multiplexer_1_out), .CLK(clk), .LOAD(cu_1_pcld), .INC(cu_1_pc_plus_plus), .OUTPUT(pc_1_output));
  REGBANK regbank_1 (
    .LOAD(cu_1_regld), .DataIn(Dout), .regSelect(n12bitreg_1_output[2:0]), .sti(cu_1_sti), .cli(cu_1_cli),
    .flagload(cu_1_flagload), .CLK(clk), .SP_plus_plus(cu_1_sp_plus_plus), .zf(alu_1_zf),
    .zfload(cu_1_zfload), .Reg0(regbank_1_reg0), .Reg1(regbank_1_reg1), .Reg2(regbank_1_reg2),
    .Reg3(regbank_1_reg3), .Reg4(regbank_1_reg4), .Reg5(regbank_1_reg5), .Reg6(regbank_1_reg6),
    .Reg7({regbank_1_reg7_2, regbank_1_reg7}), .zfout(regbank_1_zfout), .IF(regbank_1_if),
    .SP_minus_minus(cu_1_sp_minus_minus));
  Multiplexer #(.select(3), .width(16), .enable("false")) multiplexer_3 (
    .in0(Din), .in1(multiplexer_4_out), .in2({multiplexer_5_out_2, multiplexer_5_out}), .in3(alu_1_output),
    .in4({4'b0000, pc_1_output}), .in5(regbank_1_reg6), .out(Dout), .sel(cu_1_mux0));  // open: in6, in7
  Multiplexer #(.select(3), .width(16), .enable("false")) multiplexer_4 (
    .in0(regbank_1_reg0), .in1(regbank_1_reg1), .in2(regbank_1_reg2), .in3(regbank_1_reg3),
    .in4(regbank_1_reg4), .in5(regbank_1_reg5), .in6(regbank_1_reg6),
    .in7({regbank_1_reg7_2, regbank_1_reg7}), .out(multiplexer_4_out), .sel(n12bitreg_1_output[8:6]));
  _12BITREG u_12bitreg_1 (.INPUT(Din[11:0]), .CLK(clk), .LOAD(cu_1_irld), .OUTPUT(n12bitreg_1_output));
  ALU alu_1 (
    .INPUT1(multiplexer_4_out), .INPUT2({multiplexer_5_out_2, multiplexer_5_out}),
    .ALUOP(n12bitreg_1_output[11:6]), .ZF(alu_1_zf), .OUTPUT(alu_1_output));
  Multiplexer #(.select(3), .width(16), .enable("false")) multiplexer_5 (
    .in0(regbank_1_reg0), .in1(regbank_1_reg1), .in2(regbank_1_reg2), .in3(regbank_1_reg3),
    .in4(regbank_1_reg4), .in5(regbank_1_reg5), .in6(regbank_1_reg6),
    .in7({regbank_1_reg7_2, regbank_1_reg7}), .out({multiplexer_5_out_2, multiplexer_5_out}),
    .sel(n12bitreg_1_output[5:3]));
  Adder #(.width(16)) adder_2 (.a(16'h7f0), .b(Din), .out(adder_2_out));  // open: cin, cout
  \_16BİTREG  \u_16bi̇treg_1  (
    .INPUT(adder_2_out), .CLK(clk), .LOAD(cu_1_intload), .OUTPUT({n16bi_treg_1_output_2, n16bi_treg_1_output}));
  cu cu_1 (
    .Din(Din), .ZF(regbank_1_zfout), .IF(regbank_1_if), .INT(\int ), .clk(clk), .ARMUX0(cu_1_armux0[0]),
    .ARMUX1(cu_1_armux0[1]), .PcLD(cu_1_pcld), .PC_plus_plus(cu_1_pc_plus_plus), .MEMLD(memload),
    .REGLD(cu_1_regld), .zfload(cu_1_zfload), .MUX0(cu_1_mux0[0]), .MUX1(cu_1_mux0[1]), .MUX2(cu_1_mux0[2]),
    .SP_minus_minus(cu_1_sp_minus_minus), .SP_plus_plus(cu_1_sp_plus_plus), .IRLD(cu_1_irld),
    .RETMUX(cu_1_retmux), .intload(cu_1_intload), .flagload(cu_1_flagload), .sti(cu_1_sti), .cli(cu_1_cli),
    .intack(intack));  // open: FETCH
endmodule

module interruptinput (
  input  [15:0] Din,
  input  ready,
  input  [11:0] Addr,
  output [15:0] Dout,
  output \int 
);

  wire and_1_out, not_1_out, undriven;

  not not_1 (not_1_out, ready);
  S_R_Flip_Flop s_r_ff_1 (
    .S(ready), .clk(ready), .R(not_1_out), .Q(\int ), .preset(undriven), .reset(and_1_out), .en(1'b1));  // open: Qn
  \_16BİTREG  \u_16bi̇treg_1  (.INPUT(Din), .CLK(ready), .LOAD(1'b1), .OUTPUT(Dout));
  and and_1 (and_1_out, Addr[11], ~Addr[10], Addr[9], ~Addr[8], ~Addr[7], ~Addr[6], ~Addr[5], ~Addr[4], ~Addr[3], ~Addr[2], ~Addr[1], ~Addr[0]);  // AND_Gate
endmodule

module polling (
  input  [15:0] Din,
  input  ready,
  input  [11:0] Addr,
  output [15:0] Dout
);

  wire _900_1_out, and_1_out;
  wire [0:0] s_r_ff_1_q;
  wire [15:0] n16bi_treg_1_output;

  \_16BİTREG  \u_16bi̇treg_1  (.INPUT(Din), .CLK(s_r_ff_1_q[0]), .LOAD(s_r_ff_1_q[0]), .OUTPUT(n16bi_treg_1_output));
  S_R_Flip_Flop s_r_ff_1 (.S(1'b0), .clk(ready), .Q(s_r_ff_1_q[0]), .reset(and_1_out));  // open: R, Qn, preset, en
  and and_1 (and_1_out, ~Addr[0], _900_1_out);  // AND_Gate
  Multiplexer #(.width(16), .enable("false")) multiplexer_1 (
    .in0(n16bi_treg_1_output), .in1({{15{1'b0}}, s_r_ff_1_q[0]}), .out(Dout), .sel(Addr[0]));
  and _900_1 (_900_1_out, Addr[11], ~Addr[10], ~Addr[9], Addr[8], ~Addr[7], ~Addr[6], ~Addr[5], ~Addr[4], ~Addr[3], ~Addr[2], ~Addr[1]);  // AND_Gate
endmodule

module clock (
  input  clk,
  output \int ,
  output [15:0] \output 
);

  wire not_1_out;
  wire [15:0] adder_1_out, multiplexer_1_out, n16bi_treg_1_output;

  not not_1 (not_1_out, \int );
  Multiplexer #(.width(16), .enable("false")) multiplexer_1 (
    .in0({16{1'b0}}), .in1(adder_1_out), .out(multiplexer_1_out), .sel(not_1_out));
  Adder #(.width(16)) adder_1 (.a(n16bi_treg_1_output), .b(16'h1), .out(adder_1_out));  // open: cin, cout
  \_16BİTREG  \u_16bi̇treg_1  (.INPUT(multiplexer_1_out), .CLK(clk), .LOAD(1'b1), .OUTPUT(n16bi_treg_1_output));
  \_16BİTREG  \u_16bi̇treg_2  (.INPUT(adder_1_out), .CLK(clk), .LOAD(1'b1), .OUTPUT(\output ));
  and and_1 (\int , ~n16bi_treg_1_output[0], ~n16bi_treg_1_output[1], ~n16bi_treg_1_output[2], ~n16bi_treg_1_output[3], ~n16bi_treg_1_output[4], ~n16bi_treg_1_output[5], ~n16bi_treg_1_output[6], ~n16bi_treg_1_output[7], ~n16bi_treg_1_output[8], ~n16bi_treg_1_output[9], n16bi_treg_1_output[10], ~n16bi_treg_1_output[11], ~n16bi_treg_1_output[12], ~n16bi_treg_1_output[13], ~n16bi_treg_1_output[14], ~n16bi_treg_1_output[15]);  // AND_Gate
endmodule

// pic
module PIC (
  input  input1,
  input  input2,
  output active,
  output [15:0] PicOut
);

  wire priority_encoder_1_en_out;

  Priority_Encoder priority_encoder_1 (
    .in3(input1), .in6(input2), .out(PicOut[2:0]), .en_out(priority_encoder_1_en_out));  // open: in0, in1, in2, in4, in5, in7, en_in, gs
  not not_1 (active, priority_encoder_1_en_out);

  assign PicOut[15:3] = {13{1'b0}};
endmodule

module cu2 (
  input  [15:0] Din,
  input  ZF,
  input  IF,
  input  INT,
  input  clk,
  output FETCH,
  output ARMUX0,
  output ARMUX1,
  output PcLD,
  output PC_plus_plus,
  output MEMLD,
  output REGLD,
  output zfload,
  output MUX0,
  output MUX1,
  output MUX2,
  output SP_minus_minus,
  output SP_plus_plus,
  output IRLD,
  output RETMUX,
  output intload,
  output flagload,
  output sti,
  output cli,
  output intack
);

  wire and_1_out, and_3_out;
  wire [0:0] and_2_out;
  wire [3:0] multiplexer_1_out;
  wire [5:0] multiplexer_2_out, multiplexer_3_out, n6bitreg_1_output, rom_1_data;

  and and_1 (and_1_out, ~rom_1_data[0], ~rom_1_data[1], ~rom_1_data[2], ~rom_1_data[3], ~rom_1_data[4], ~rom_1_data[5]);  // AND_Gate
  and and_2 (and_2_out[0], ~Din[12], ~Din[13], Din[14], ~Din[15]);  // AND_Gate
  and and_3 (and_3_out, IF, INT, and_1_out);
  Multiplexer #(.select(2), .width(4), .enable("false")) multiplexer_1 (
    .in0(Din[15:12]), .in1(Din[15:12]), .in2(4'b0000), .in3(4'b0101), .out(multiplexer_1_out),
    .sel({ZF, and_2_out[0]}));
  Multiplexer #(.width(6), .enable("false")) multiplexer_2 (
    .in0({2'b00, multiplexer_1_out}), .in1(rom_1_data), .out(multiplexer_2_out), .sel(FETCH));
  Multiplexer #(.width(6), .enable("false")) multiplexer_3 (
    .in0(multiplexer_2_out), .in1(6'b001101), .out(multiplexer_3_out), .sel(and_3_out));
  _6bitreg u_6bitreg_1 (.INPUT(multiplexer_3_out), .CLK(clk), .LOAD(1'b1), .OUTPUT(n6bitreg_1_output));
  ROM #(.addrWidth(6), .dataWidth(26)) rom_1 (
    .addr(n6bitreg_1_output),
    .data({FETCH, ARMUX0, ARMUX1, PcLD, PC_plus_plus, MEMLD, REGLD, zfload, MUX0, MUX1, MUX2, SP_minus_minus, SP_plus_plus, IRLD, RETMUX, intload, flagload, sti, cli, intack, rom_1_data}));  // open: sel

  // Notes on the sheet:
  //   contents of rom_1 (hex, n*v repeats v):
  //   2201000 0 280000 0 1080000 0 1120000 0 0 0 400000 0 0 0 f0000 0 924000 0 201e 0 d0c000 0 2020 0 100
  //   0 80 0 2022 0 880000 0 c00800 0 c02824 0 800200 0 92c028 0 90c46a 0 1c00880
endmodule

module _6bitreg (
  input  [5:0] INPUT,
  input  CLK,
  input  LOAD,
  output [5:0] OUTPUT
);

  wire not_1_out, not_2_out, not_3_out, not_4_out, not_5_out, not_6_out;

  S_R_Flip_Flop s_r_ff_1 (.S(INPUT[0]), .clk(CLK), .R(not_1_out), .Q(OUTPUT[0]));  // open: Qn, preset, reset, en
  not not_1 (not_1_out, INPUT[0]);
  S_R_Flip_Flop s_r_ff_2 (.S(INPUT[1]), .clk(CLK), .R(not_2_out), .Q(OUTPUT[1]), .en(LOAD));  // open: Qn, preset, reset
  not not_2 (not_2_out, INPUT[1]);
  S_R_Flip_Flop s_r_ff_3 (.S(INPUT[2]), .clk(CLK), .R(not_3_out), .Q(OUTPUT[2]), .en(LOAD));  // open: Qn, preset, reset
  not not_3 (not_3_out, INPUT[2]);
  S_R_Flip_Flop s_r_ff_4 (.S(INPUT[3]), .clk(CLK), .R(not_4_out), .Q(OUTPUT[3]), .en(LOAD));  // open: Qn, preset, reset
  not not_4 (not_4_out, INPUT[3]);
  S_R_Flip_Flop s_r_ff_5 (.S(INPUT[4]), .clk(CLK), .R(not_5_out), .Q(OUTPUT[4]), .en(LOAD));  // open: Qn, preset, reset
  not not_5 (not_5_out, INPUT[4]);
  S_R_Flip_Flop s_r_ff_6 (.S(INPUT[5]), .clk(CLK), .R(not_6_out), .Q(OUTPUT[5]), .en(LOAD));  // open: Qn, preset, reset
  not not_6 (not_6_out, INPUT[5]);
endmodule
